# Fritzing sketch mega2wdSteer (saved by Fritzing 0.9.3b)

parts:
  Part1 = Arduino Mega 2560 (Rev3)
  L298N1 = L298N DC motor driver
  DC_right_rear = DC Motor  # not connected
  DC_left_rear = DC Motor  # not connected
  hc-sr04_right_front = hc-sr04
  hc-sr04_left_front = hc-sr04
  steering_servo = Basic Servo
  front_IR = 4 channel IR obstacle detector FC-35
  side_IR = 4 channel IR obstacle detector FC-35  # not connected

nets:
  N1: Part1.A12, front_IR.IN1
  N2: Part1.D10_PWM, L298N1.ENA
  N3: Part1.D9_PWM, L298N1.IN1
  N4: Part1.D8_PWM, L298N1.IN2
  N5: Part1.D3_PWM, steering_servo.pulse
  N6: Part1.D5_PWM, L298N1.ENB
  N7: Part1.D6_PWM, L298N1.IN3
  N8: Part1.D7_PWM, L298N1.IN4
  N9: Part1.D34, hc-sr04_right_front.Trig
  N10: Part1.D36, hc-sr04_right_front.Echo
  N11: Part1.D38, hc-sr04_left_front.Trig
  N12: Part1.D40, hc-sr04_left_front.Echo

custom parts:
  L298N DC motor driver: 2x DC motor driver with 78M05 positive voltage regulator (7..35 V) L298N: max 46 V, 2 A Set 5 V Enable jumper to enable 5 V regultor (needed for the L298N) and +5 V output at screw terminal or supply external +5 V at screw terminal Set ENA and/or ENB to +5 V to enable motor permanently or supply ENA and/or ENB with PWM signal IN1 and IN2 set rotation directory for motor A (OUT1/OUT2) IN2 and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
  4 channel IR obstacle detector FC-35: Detector de obstáculos IR
